# Fritzing sketch LED array (saved by Fritzing 0.7.12b)
breadboards: 1

parts:
  LED1 = LED - 5mm [color="Green (570nm)" package="5 mm [THT]"]
  LED2 = LED - 5mm [color="Green (570nm)" package="5 mm [THT]"]
  LED3 = LED - 5mm [color="Green (570nm)" package="5 mm [THT]"]
  R1 = Resistor [tolerance=±5% resistance=220 package=THT]
  LED4 = LED - 5mm [color="Green (570nm)" package="5 mm [THT]"]
  LED5 = LED - 5mm [color="Green (570nm)" package="5 mm [THT]"]
  LED6 = LED - 5mm [color="Green (570nm)" package="5 mm [THT]"]
  R2 = Resistor [tolerance=±5% resistance=220 package=THT]

nets:
  N1: LED1.cathode, LED2.anode
  9V: LED1.anode, LED4.anode
  N2: LED2.cathode, LED3.anode
  N3: LED3.cathode, R1.Pin_0
  GND: R1.Pin_1, R2.Pin_1
  N4: LED4.cathode, LED6.anode
  N5: LED5.cathode, R2.Pin_0
  N6: LED5.anode, LED6.cathode

notes:
  The RADAR display has 1 LED in the middle and 7 6-LED arrays like this, controlled by the outputs of one shift register.
