# Fritzing sketch MissionControl-Arduino-IO (saved by Fritzing 0.7.12b)
breadboards: 1

parts:
  Arduino1 = Arduino
  Black = Rotary Potentiometer (Small) [maximum_resistance=100kΩ]
  Silver = Rotary Potentiometer (Small) [maximum_resistance=100kΩ]
  Launch = Pushbutton [package=THT]
  Green = Pushbutton [package=THT]
  Red = Pushbutton [package=THT]
  Key = Toggle Switch [package=THT]
  Arm = Toggle Switch [package=THT]
  Left = Toggle Switch [package=THT]
  Right = Toggle Switch [package=THT]
  Yellow = Pushbutton [package=THT]
  SPKR1 = Loudspeaker
  RGB_Left = RGB LED (com. anode, rbg) [package="5 mm [THT]"]
  Power = Toggle Switch [package=THT]
  R1 = Resistor [tolerance=±5% resistance=220 package=THT]
  R2 = Resistor [tolerance=±5% resistance=220 package=THT]
  R3 = Resistor [tolerance=±5% resistance=220 package=THT]
  DC_Power1 = DC Power [voltage=5]

nets:
  GND: Arduino1.GND, Black.leg1, Silver.leg1, Launch.leg0, Green.leg0, Red.leg0, Yellow.leg0, SPKR1.pin2, RGB_Left.common_anode, DC_Power1.V+
  N1: Arduino1.D13, SPKR1.pin1
  N2: Arduino1.D12, Right.COM
  N3: Arduino1.D11, Arm.COM
  N4: Arduino1.D10, R2.Pin_1
  N5: Arduino1.D9, R3.Pin_1
  N6: Arduino1.D5, R1.Pin_1
  N7: Arduino1.D3, Key.COM
  N8: Arduino1.D2, Left.COM
  N9: Arduino1.VIN, Power.COM
  N10: Arduino1.A0, Black.wiper
  N11: Arduino1.A1, Launch.leg1
  N12: Arduino1.A2, Yellow.leg1
  N13: Arduino1.A3, Red.leg1
  N14: Arduino1.A4, Green.leg1
  N15: Arduino1.A5, Silver.wiper
  5V: Black.leg2, Silver.leg2
  N16: RGB_Left.red_cathode, R1.Pin_0
  N17: RGB_Left.blue_cathode, R3.Pin_0
  N18: RGB_Left.green_cathode, R2.Pin_0
  N19: Power.L1, DC_Power1.GND

notes:
  This generally shows the inputs and outputs that are connected to the Arduino.
  Ignore the resistor values and the breadboard/pcb views.
  Buttons and switches connect GND to Arduino inputs with pull-up resistors enabled, so "on" = logic low.
  One RGB LED is driven by PWM pins.
  The other outputs (16-segment LED, launch button LED, and "radar" LED array) are switched by shift registers. None are pictured here. The shift registers use pins 4, 7, and 8.
