# Fritzing sketch MissionControl-ShiftRegisters (saved by Fritzing 0.7.12b)
breadboards: 1

parts:
  TPIC6B1 = TPIC6B595
  Arduino1 = Arduino
  TPIC6B2 = TPIC6B595

nets:
  N1: TPIC6B1.SER_IN, Arduino1.D8
  5V: TPIC6B1.SRCLR, TPIC6B2.SRCLR
  GND: TPIC6B1.G, TPIC6B2.G
  N2: TPIC6B1.RCK, Arduino1.D4, TPIC6B2.RCK
  N3: TPIC6B1.SRCK, Arduino1.D7, TPIC6B2.SRCK
  N4: TPIC6B1.SER_OUT, TPIC6B2.SER_IN

notes:
  The Fritzing part I found for the TPIC6B595 shift register seems to insist on connecting Vcc to the "NC" pin 20. Ignore that.
  Not shown:
  Vcc is +5v
  Connect GND appropriately
  Each DRAINx sinks current from the output devices.
  The 16-segment LED is connected to a common +5v supply, and each pin on the display goes through a current-liminting resistor and then to the DRAINx pin on the shift register.
  The launch button LED and the "Radar" LED array are connected to +9v.
  SER OUT goes to SER IN on the next shift register. The first register has SER IN connected to pin 8.
  SRCK on each register goes to Arduino pin 7.
  RCK on each register goes to pin 4.

custom parts:
  TPIC6B595: This is an 8-Bit shift register able to take high-voltages
